# Fritzing sketch schema (saved by Fritzing 0.9.3b)
breadboards: 3

parts:
  Onderdeel2 = Arduino Nano (Rev3.0)
  RHT1 = Humidity and Temperature Sensor RHT03
  IC1 = SHIFT REGISTER [package=dil16]
  IC2 = SHIFT REGISTER [package=dil16]
  R1 = Resistor [tolerance=±5% resistance=220 package=THT]
  R2 = Resistor [tolerance=±5% resistance=220 package=THT]
  R3 = Resistor [tolerance=±5% resistance=220 package=THT]
  R4 = Resistor [tolerance=±5% resistance=220 package=THT]
  R5 = Resistor [tolerance=±5% resistance=220 package=THT]
  R6 = Resistor [tolerance=±5% resistance=220 package=THT]
  R7 = Resistor [tolerance=±5% resistance=220 package=THT]
  R8 = Resistor [tolerance=±5% resistance=220 package=THT]
  Disp1 = LBT2088AH [part_number=LBT2088AH]

nets:
  GND: Onderdeel2.GND, RHT1.GND_2, IC1.GND, IC1.G, IC2.GND, IC2.G
  N1: Onderdeel2.D6, RHT1.Data-signal
  N2: Onderdeel2.A2, IC1.SCK, IC2.SCK
  N3: Onderdeel2.A1, IC1.RCK, IC2.RCK
  N4: Onderdeel2.A0, IC2.SER
  VCC: Onderdeel2.3V3, RHT1.Vcc, IC1.SCL, IC1.VCC, IC2.SCL, IC2.VCC
  N5: IC1.QB, R7.Pin_1
  N6: IC1.QC, R6.Pin_1
  N7: IC1.QD, R5.Pin_1
  N8: IC1.QE, R4.Pin_1
  N9: IC1.QF, R3.Pin_1
  N10: IC1.QG, R2.Pin_1
  N11: IC1.QH, R1.Pin_1
  N12: IC1.SER, IC2.QH*
  N13: IC1.QA, R8.Pin_1
  N14: IC2.QB, Disp1.pin_3
  N15: IC2.QC, Disp1.pin_4
  N16: IC2.QD, Disp1.pin_10
  N17: IC2.QE, Disp1.pin_6
  N18: IC2.QF, Disp1.pin_11
  N19: IC2.QG, Disp1.pin_15
  N20: IC2.QH, Disp1.pin_16
  N21: IC2.QA, Disp1.pin_13
  N22: R1.Pin_0, Disp1.pin_5
  N23: R2.Pin_0, Disp1.pin2
  N24: R3.Pin_0, Disp1.pin_7
  N25: R4.Pin_0, Disp1.pin1
  N26: R5.Pin_0, Disp1.pin_12
  N27: R6.Pin_0, Disp1.pin_8
  N28: R7.Pin_0, Disp1.pin_14
  N29: R8.Pin_0, Disp1.pin_9
