# Fritzing sketch schema (saved by Fritzing 0.9.3b)
breadboards: 1

parts:
  Onderdeel2 = Arduino Nano (Rev3.0)
  U1 = 7-SEGMENT-DISPLAY [package=7-segment-display]
  U2 = 7-SEGMENT-DISPLAY [package=7-segment-display]
  R1 = Resistor [tolerance=±5% resistance=220 package=THT]

nets:
  N1: Onderdeel2.D1/TX, U2.G2
  N2: Onderdeel2.D0/RX, U2.F
  N3: Onderdeel2.D2, U2.C
  N4: Onderdeel2.D3, U2.D
  N5: Onderdeel2.D4, U1.B
  N6: Onderdeel2.D5, U2.G
  N7: Onderdeel2.D6, U2.G1
  N8: Onderdeel2.5V, U1.A, U2.E, R1.Pin_0, R1.Pin_1
