# Fritzing sketch schema (saved by Fritzing 0.9.3b)
breadboards: 3

parts:
  Onderdeel2 = Arduino Nano (Rev3.0)
  Disp1 = LBT2088AH [part_number=LBT2088AH]
  R1 = Resistor [tolerance=±5% resistance=220 package=THT]
  R2 = Resistor [tolerance=±5% resistance=220 package=THT]
  R3 = Resistor [tolerance=±5% resistance=220 package=THT]
  R4 = Resistor [tolerance=±5% resistance=220 package=THT]
  R5 = Resistor [tolerance=±5% resistance=220 package=THT]
  R6 = Resistor [tolerance=±5% resistance=220 package=THT]
  S1 = Pushbutton [package="[THT]"]

nets:
  N1: Onderdeel2.GND, S1.Pin_1, S1.Pin_2
  N2: Onderdeel2.D2, R1.Pin_1
  N3: Onderdeel2.D3, R2.Pin_1
  N4: Onderdeel2.D4, R3.Pin_1
  N5: Onderdeel2.D5, R4.Pin_1
  N6: Onderdeel2.D6, R5.Pin_1
  N7: Onderdeel2.D7, R6.Pin_1
  N8: Onderdeel2.D8, S1.Pin_3, S1.Pin_4
  N9: Onderdeel2.A5, Disp1.pin_16
  N10: Onderdeel2.A4, Disp1.pin_15
  N11: Onderdeel2.A3, Disp1.pin_6
  N12: Onderdeel2.A2, Disp1.pin_10
  N13: Onderdeel2.A1, Disp1.pin_3
  N14: Onderdeel2.A0, Disp1.pin_13
  N15: Disp1.pin1, R4.Pin_0
  N16: Disp1.pin2, R5.Pin_0
  N17: Disp1.pin_5, R6.Pin_0
  N18: Disp1.pin_9, R1.Pin_0
  N19: Disp1.pin_12, R3.Pin_0
  N20: Disp1.pin_14, R2.Pin_0
