# Fritzing sketch schema (saved by Fritzing 0.9.3b)
breadboards: 1

parts:
  Onderdeel2 = Arduino Nano (Rev3.0)
  SP1 = SPEAKER [package=pcb_mount_speaker]
  R1 = Rotary Potentiometer (Small) [maximum_resistance=100kΩ package=THT]

nets:
  N1: Onderdeel2.GND, SP1.+, R1.leg1
  N2: Onderdeel2.5V, R1.leg2
  N3: Onderdeel2.A0, R1.wiper
  N4: Onderdeel2.D13/SCK, SP1.-
