# Fritzing sketch schema (saved by Fritzing 0.9.3b)
breadboards: 1

parts:
  Onderdeel2 = Arduino Nano (Rev3.0)
  LED1 = LED - 5mm [color="Blue (470nm)" package="5 mm [THT]"]
  R1 = Resistor [tolerance=±5% resistance=220 package=THT]

nets:
  N1: Onderdeel2.GND, LED1.cathode
  N2: Onderdeel2.D13/SCK, R1.Pin_0
  N3: LED1.anode, R1.Pin_1
