# Fritzing sketch schema (saved by Fritzing 0.9.3b)
breadboards: 1

parts:
  Onderdeel2 = Arduino Nano (Rev3.0)
  R1 = Resistor [tolerance=±5% resistance=220 package=THT]
  R2 = Resistor [tolerance=±5% resistance=220 package=THT]
  R3 = Resistor [tolerance=±5% resistance=220 package=THT]
  LED1 = RGB LED - (4 legs) [package="5 mm [THT]"]

nets:
  N1: Onderdeel2.D9, R3.Pin_1
  N2: Onderdeel2.D10, R2.Pin_1
  N3: Onderdeel2.D11/MOSI, R1.Pin_1
  N4: Onderdeel2.5V, LED1.common_anode
  N5: R1.Pin_0, LED1.blue_cathode
  N6: R2.Pin_0, LED1.green_cathode
  N7: R3.Pin_0, LED1.red_cathode
