# Fritzing sketch schema (saved by Fritzing 0.9.3b)
breadboards: 1

parts:
  Onderdeel2 = Arduino Nano (Rev3.0)
  R1 = Rotary Potentiometer (Small) [maximum_resistance=100kΩ package=THT]
  LCD1 = LCD screen

nets:
  GND: Onderdeel2.GND, R1.leg2, LCD1.VSS, LCD1.R/W
  5V: Onderdeel2.5V, R1.leg1, LCD1.VDD
  N1: Onderdeel2.A5, LCD1.E
  N2: Onderdeel2.A4, LCD1.RS
  N3: Onderdeel2.A3, LCD1.DB7
  N4: Onderdeel2.A2, LCD1.DB6
  N5: Onderdeel2.A1, LCD1.DB5
  N6: Onderdeel2.A0, LCD1.DB4
  N7: R1.wiper, LCD1.V0
